# Fritzing sketch Schematic (saved by Fritzing 0.9.3b)
circuit board: 8.46667cm x 5.64444cm
breadboards: 1

parts:
  U1 = NodeMCU V3.0
  LED1 = LED - 5mm [color="Infrared (940nm)" current=50mA package="5 mm [THT]"]
  R1 = Resistor [tolerance=±5% resistance=47 package=THT]
  R2 = Resistor [tolerance=±5% resistance=330 package=THT]
  U2 = mystery part, 3 pins [chip_label=DHT11]
  Q1 = NPN-Transistor [package="TO92 [THT]"]

nets:
  N1: U1.D2, R2.Pin_1
  N2: U1.D3, U2.pin2
  N3: U1.3V3, R1.Pin_1, U2.pin1
  N4: U1.GND#6, U1.GND#13, U1.GND#16, U1.GND#33, U2.pin3, Q1.E
  N5: LED1.cathode, Q1.C
  N6: LED1.anode, R1.Pin_0
  N7: R2.Pin_0, Q1.B

custom parts:
  NodeMCU V3.0: ESP8266 based NodeMCU
